// Digital circuit CPU.dig as structural Verilog
// The RUN1920 CPU component
module CPU (
  input  [31:0] DATABUS_IN,
  input  CLOCK,
  input  nRESET,
  output [31:0] ADDRESSBUS,
  output [31:0] DATABUS_OUT,
  output nRE,
  output nWE,
  output HALTED
);

  wire ALU_carry_out, ALU_negative, ALU_overflow, ALU_zero, FlagRegisterBank_p8, FlagRegisterBank_p9,
       FlagRegisterBank_p10, FlagRegisterBank_p11, InstructionDecoder_carry, InstructionDecoder_halt,
       InstructionDecoder_nread, InstructionDecoder_nwrite, InstructionDecoder_pop, InstructionDecoder_push,
       InstructionDecoder_setflags, InstructionDecoder_use_constant, not_3_out, or_1_out, or_2_out, or_3_out,
       or_4_out, regre_1_p1, regre_1_p4, Tester_testsucceeds, Timer_fetch;
  wire [2:0] InstructionDecoder_opcode;
  wire [3:0] InstructionDecoder_addr_a, InstructionDecoder_addr_b, InstructionDecoder_addr_dest,
       InstructionDecoder_condition, multiplexer_1_out;
  wire [31:0] InstructionDecoder_constant, multiplexer_2_out, multiplexer_3_out, RegisterBank_reg_a,
       RegisterBank_reg_b, regre_1_p5;

  // RegRE #(.Bits(32)) regre_1: pin names not known; wires that end beside it: regre_1_p1, DATABUS_IN, CLOCK, regre_1_p4, regre_1_p5
  InstructionDecoder InstructionDecoder (
    .INSTRUCTION(regre_1_p5), .nWRITE(InstructionDecoder_nwrite), .PUSH(InstructionDecoder_push),
    .nREAD(InstructionDecoder_nread), .POP(InstructionDecoder_pop), .ADDR_DEST(InstructionDecoder_addr_dest),
    .ADDR_B(InstructionDecoder_addr_b), .ADDR_A(InstructionDecoder_addr_a),
    .CONSTANT(InstructionDecoder_constant), .USE_CONSTANT(InstructionDecoder_use_constant),
    .Carry(InstructionDecoder_carry), .OPCODE(InstructionDecoder_opcode),
    .SETFLAGS(InstructionDecoder_setflags), .CONDITION(InstructionDecoder_condition),
    .HALT(InstructionDecoder_halt));
  Multiplexer #(.Bits(4)) multiplexer_1 (
    .sel(Timer_fetch), .in_0(InstructionDecoder_addr_a), .in_1(4'b1111), .out(multiplexer_1_out));
  or or_1 (or_1_out, InstructionDecoder_nwrite, InstructionDecoder_push);
  or or_2 (or_2_out, InstructionDecoder_nread, InstructionDecoder_pop);
  Timer Timer (
    .HALT(InstructionDecoder_halt), .CLOCK(CLOCK), .nRESET_IN(nRESET), .TEST_SUCCEEDS(Tester_testsucceeds),
    .EXECUTE(regre_1_p1), .FETCH(Timer_fetch), .nRESET_OUT(regre_1_p4), .HALTED(HALTED));
  RegisterBank RegisterBank (
    .DATA(DATABUS_OUT), .POP(InstructionDecoder_pop), .ADDR_DEST(InstructionDecoder_addr_dest),
    .ADDR_B(InstructionDecoder_addr_b), .ADDR_A(multiplexer_1_out), .nRESET(regre_1_p4), .CLOCK(CLOCK),
    .REG_B(RegisterBank_reg_b), .REG_A(RegisterBank_reg_a));
  Multiplexer #(.Bits(32)) multiplexer_2 (
    .sel(InstructionDecoder_use_constant), .in_0(RegisterBank_reg_a), .in_1(InstructionDecoder_constant),
    .out(multiplexer_2_out));
  ALU ALU (
    .A(RegisterBank_reg_b), .B(multiplexer_2_out), .Carry_in(InstructionDecoder_carry),
    .OPCODE(InstructionDecoder_opcode), .RESULT(DATABUS_OUT), .Overflow(ALU_overflow),
    .Negative(ALU_negative), .Carry_out(ALU_carry_out), .Zero(ALU_zero));
  // FlagRegisterBank FlagRegisterBank: pin names not known; wires that end beside it: ALU_overflow, ALU_negative, ALU_carry_out, ALU_zero, InstructionDecoder_setflags, CLOCK, regre_1_p4, FlagRegisterBank_p8, FlagRegisterBank_p9, FlagRegisterBank_p10, FlagRegisterBank_p11
  or or_3 (or_3_out, or_2_out, Timer_fetch);
  Multiplexer #(.Bits(32)) multiplexer_3 (
    .sel(Timer_fetch), .in_0(RegisterBank_reg_a), .in_1(DATABUS_OUT), .out(multiplexer_3_out));
  not not_1 (nWE, or_1_out);
  not not_2 (nRE, or_3_out);
  or or_4 (or_4_out, nWE, nRE);
  not not_3 (not_3_out, or_4_out);
  Multiplexer #(.Bits(32)) multiplexer_4 (
    .sel(not_3_out), .in_0(multiplexer_3_out), .in_1({32{1'b0}}), .out(ADDRESSBUS));
  Tester Tester (
    .Overflow(FlagRegisterBank_p8), .Negative(FlagRegisterBank_p9), .Carry(FlagRegisterBank_p10),
    .Zero(FlagRegisterBank_p11), .Condition(InstructionDecoder_condition), .TestSucceeds(Tester_testsucceeds));
endmodule
