// Digital circuit InstructionDecoder.dig as structural Verilog
// The RUN1920 CPU InstructionDecoder component
module InstructionDecoder (
  input  [31:0] INSTRUCTION,
  output nWRITE,
  output PUSH,
  output nREAD,
  output POP,
  output [3:0] ADDR_DEST,
  output [3:0] ADDR_B,
  output [3:0] ADDR_A,
  output [31:0] CONSTANT,
  output USE_CONSTANT,
  output Carry,
  output [2:0] OPCODE,
  output SETFLAGS,
  output [3:0] CONDITION,
  output HALT
);

  wire and_1_out, comparator_2_eq, comparator_5_eq, comparator_7_eq, comparator_8_eq, nor_1_out, or_2_out;
  wire [31:0] c10toc32_1_c32, c22toc32_1_c32, multiplexer_2_out;

  Multiplexer #(.Bits(3)) multiplexer_1 (.sel(INSTRUCTION[31]), .in_0(INSTRUCTION[30:28]), .in_1(3'b110), .out(OPCODE));
  Comparator #(.Bits(4)) comparator_1 (.a(INSTRUCTION[3:0]), .b(4'b0010), .eq(Carry));  // open: gt, lt
  and and_1 (and_1_out, ~INSTRUCTION[31], INSTRUCTION[27]);  // And
  Comparator #(.Bits(32)) comparator_2 (.a(INSTRUCTION), .b({32{1'b0}}), .eq(comparator_2_eq));  // open: gt, lt
  Comparator #(.Bits(6)) comparator_3 (.a(INSTRUCTION[31:26]), .b({6{1'b1}}), .eq(HALT));  // open: gt, lt
  Comparator #(.Bits(6)) comparator_4 (.a(INSTRUCTION[31:26]), .b(6'b110100), .eq(POP));  // open: gt, lt
  Comparator #(.Bits(6)) comparator_5 (.a(INSTRUCTION[31:26]), .b(6'b110000), .eq(comparator_5_eq));  // open: gt, lt
  Comparator #(.Bits(6)) comparator_6 (.a(INSTRUCTION[31:26]), .b(6'b110001), .eq(PUSH));  // open: gt, lt
  Comparator #(.Bits(6)) comparator_7 (.a(INSTRUCTION[31:26]), .b(6'b111000), .eq(comparator_7_eq));  // open: gt, lt
  nor nor_1 (nor_1_out, INSTRUCTION[31], INSTRUCTION[26]);
  Comparator #(.Bits(2)) comparator_8 (.a(2'b10), .b(INSTRUCTION[31:30]), .eq(comparator_8_eq));  // open: gt, lt
  C10toC32 c10toc32_1 (.C10(INSTRUCTION[25:16]), .C32(c10toc32_1_c32));
  C22toC32 c22toc32_1 (.C22(INSTRUCTION[29:8]), .C32(c22toc32_1_c32));
  or or_1 (SETFLAGS, and_1_out, INSTRUCTION[31], comparator_2_eq);
  or or_2 (or_2_out, comparator_5_eq, comparator_7_eq, nor_1_out);
  or or_3 (nREAD, POP, comparator_5_eq);
  or or_4 (nWRITE, PUSH, comparator_7_eq);
  Multiplexer #(.Bits(32)) multiplexer_2 (
    .sel(or_2_out), .in_0({32{1'b0}}), .in_1(c10toc32_1_c32), .out(multiplexer_2_out));
  Multiplexer #(.Bits(32)) multiplexer_3 (
    .sel(comparator_8_eq), .in_0(multiplexer_2_out), .in_1(c22toc32_1_c32), .out(CONSTANT));
  or or_5 (USE_CONSTANT, or_2_out, comparator_8_eq);

  assign ADDR_A = INSTRUCTION[15:12];
  assign ADDR_B = INSTRUCTION[11:8];
  assign ADDR_DEST = INSTRUCTION[7:4];
  assign CONDITION = INSTRUCTION[3:0];
endmodule
